// Logisim project Team Assignment 01.circ as structural Verilog
module Couches__AND_GATE (
  input  in_1,
  input  in_2,
  output out_3
);

  and and_1 (out_3, in_1, in_2);

  // Notes on the sheet:
  //   Two Couches
endmodule

module Study_Table___OR_GATE (
  input  in_1,
  output out_2
);

  or or_1 (out_2, in_1, in_1);

  // Notes on the sheet:
  //   A Study Table
endmodule
