// Logisim project Lab2 Supplementary Resource.circ as structural Verilog: 1 circuit, main circuit main
module main (
  input  in_1,
  input  in_2,
  input  in_3,
  input  in_4,
  output out_5,
  output out_6
);

  wire nand_1_out, nand_2_out, nand_3_out, nor_1_out, nor_2_out, nor_3_out, nor_4_out;

  nand nand_1 (nand_1_out, in_1, in_2);
  nor nor_1 (nor_1_out, in_3, in_3);
  nor nor_2 (nor_2_out, in_4, in_4);
  nor nor_3 (nor_3_out, in_3, in_4);
  nand nand_2 (nand_2_out, in_1, nand_1_out);
  nand nand_3 (nand_3_out, nand_1_out, in_2);
  nand nand_4 (out_5, nand_2_out, nand_3_out);
  nor nor_4 (nor_4_out, nor_1_out, nor_2_out);
  nor nor_5 (out_6, nor_4_out, nor_3_out);

  // Notes on the sheet:
  //   XOR Using NAND
  //   XOR Using NOR
endmodule
